# Fritzing sketch wiringdiagram (saved by Fritzing 0.9.3b)
breadboards: 1

parts:
  Part1 = Arduino Uno (Rev3)
  J1 = Infrared Proximity Sensor
  LED1 = RGB LED (com. cathode, rgb) [package="5 mm [THT]"]
  R1 = Resistor [tolerance=±5% resistance=330 package="0402 [SMD]"]
  R2 = Resistor [tolerance=±5% resistance=330 package="0402 [SMD]"]
  R3 = Resistor [tolerance=±5% resistance=330 package="0402 [SMD]"]

nets:
  N1: Part1.A0, J1.Vout
  N2: Part1.D9_PWM, R3.Pin_1
  N3: Part1.D10_PWM/SS, R2.Pin_1
  N4: Part1.D11_PWM/MOSI, R1.Pin_1
  5V: Part1.5V, J1.Vcc, LED1.common_cathode
  GND: Part1.GND, J1.GND
  N5: LED1.red_anode, R3.Pin_0
  N6: LED1.green_anode, R2.Pin_0
  N7: LED1.blue_anode, R1.Pin_0
